// Logisim project ESF.circ as structural Verilog: 13 circuits, main circuit main
module main (
  input  Clear,
  output halt,
  output [31:0] out_3,
  output [31:0] out_4
);

  wire and_1_out, and_2_out, clock_1_out, comparator_1_gt, comparator_2_lt, comparator_3_eq, comparator_4_eq,
       comparator_5_eq, comparator_6_eq, comparator_7_eq, comparator_8_eq, controlled_buffer_1_out,
       nand_1_out, nor_1_out;
  wire [2:0] counter_1_q;
  wire [3:0] counter_2_q;
  wire [4:0] counter_3_q;
  wire [15:0] keyscheduler_1_out_10, keyscheduler_1_out_11, keyscheduler_1_out_12, keyscheduler_1_out_13,
       keyscheduler_1_out_14, multiplexer_4_out, multiplexer_5_out, multiplexer_7_out, multiplexer_8_out,
       multiplexer_9_out, multiplexer_10_out, multiplexer_11_out;
  wire [31:0] Add_Round_Key_x_2, multiplexer_1_out, multiplexer_2_out, permutation_layer_1_out_2, ram_1_data,
       register_1_q, register_2_q, register_3_q, register_4_q, register_5_q, register_8_q, register_9_q,
       register_10_q, shifter_1_out, substitution_layer_1_out_2, xor_1_out;

  and and_1 (and_1_out, comparator_8_eq, clock_1_out);
  assign controlled_buffer_1_out = and_2_out ? clock_1_out : 1'bz;  // Controlled_Buffer controlled_buffer_1
  Clock clock_1 (.out(clock_1_out));
  Register #(.width(32)) register_1 (.D(xor_1_out), .en(nand_1_out), .Q(register_1_q), .clk(and_1_out));  // open: clr
  Register #(.width(32)) register_2 (
    .D(multiplexer_2_out), .en(nand_1_out), .Q(register_2_q), .clk(and_1_out));  // open: clr
  Counter #(.width(3), .max('h7), .ongoal("stay")) counter_1 (
    .Q(counter_1_q), .clk(controlled_buffer_1_out));  // open: load, D, count, carry, clr
  Counter #(.width(4), .max('hf), .ongoal("stay")) counter_2 (
    .Q(counter_2_q), .clk(clock_1_out));  // open: load, D, count, carry, clr
  Register #(.width(32)) register_3 (.D(register_5_q), .Q(register_3_q), .clk(comparator_3_eq));  // open: en, clr
  Multiplexer #(.width(32), .enable("false")) multiplexer_1 (
    .in0(register_2_q), .in1(register_3_q), .out(multiplexer_1_out), .sel(nor_1_out));
  Comparator #(.width(4), .mode("unsigned")) comparator_1 (
    .a(counter_2_q), .b(4'b0101), .gt(comparator_1_gt));  // open: eq, lt
  Comparator #(.width(4), .mode("unsigned")) comparator_2 (
    .a(counter_2_q), .b(4'b1011), .lt(comparator_2_lt));  // open: gt, eq
  Register #(.width(32)) register_4 (.D(register_5_q), .Q(register_4_q), .clk(comparator_4_eq));  // open: en, clr
  Multiplexer #(.width(32), .enable("false")) multiplexer_2 (
    .in0(register_1_q), .in1(register_4_q), .out(multiplexer_2_out), .sel(nor_1_out));
  Shifter #(.width(32), .shift("rl")) shifter_1 (.in(multiplexer_1_out), .\dist (5'b00111), .out(shifter_1_out));
  assign xor_1_out = shifter_1_out ^ permutation_layer_1_out_2;  // XOR_Gate xor_1, 32 bits wide
  RAM #(.addrWidth(3), .dataWidth(32), .bus("separate")) ram_1 (
    .addr(counter_1_q), .data(ram_1_data), .sel(1'b1), .ld(and_2_out));  // open: din, str, clk, clr
  and and_2 (and_2_out, comparator_1_gt, comparator_2_lt);
  Substitution_Layer substitution_layer_1 (.in_1(Add_Round_Key_x_2), .out_2(substitution_layer_1_out_2));
  AddRoundKey Add_Round_Key (
    .x(multiplexer_2_out), .in_2(multiplexer_4_out), .in_3(multiplexer_5_out), .x_2(Add_Round_Key_x_2));
  Register #(.width(32)) register_5 (.D(ram_1_data), .Q(register_5_q), .clk(controlled_buffer_1_out));  // open: en, clr
  Permutation_Layer permutation_layer_1 (.in_1(substitution_layer_1_out_2), .out_2(permutation_layer_1_out_2));
  Register #(.width(32)) register_6 (.D(xor_1_out), .clk(and_1_out));  // open: en, Q, clr
  Multiplexer #(.width(32), .enable("false")) multiplexer_3 (
    .in0(xor_1_out), .out(out_3), .sel(nand_1_out));  // open: in1
  Comparator #(.width(4), .mode("unsigned")) comparator_3 (
    .a(counter_2_q), .b(4'b1000), .eq(comparator_3_eq));  // open: gt, lt
  Multiplexer #(.width(16), .enable("false")) multiplexer_4 (
    .in0(keyscheduler_1_out_10), .in1(register_8_q[15:0]), .out(multiplexer_4_out), .sel(nor_1_out));
  Multiplexer #(.width(16), .enable("false")) multiplexer_5 (
    .in0(keyscheduler_1_out_11), .in1(register_9_q[31:16]), .out(multiplexer_5_out), .sel(nor_1_out));
  Register #(.width(32)) register_7 (.D(multiplexer_2_out), .clk(and_1_out));  // open: en, Q, clr
  Multiplexer #(.width(32), .enable("false")) multiplexer_6 (
    .in0(multiplexer_2_out), .out(out_4), .sel(nand_1_out));  // open: in1
  Comparator #(.width(4), .mode("unsigned")) comparator_4 (
    .a(counter_2_q), .b(4'b0111), .eq(comparator_4_eq));  // open: gt, lt
  Register #(.width(32)) register_8 (.D(register_5_q), .Q(register_8_q), .clk(comparator_7_eq));  // open: en, clr
  Register #(.width(32)) register_9 (.D(register_5_q), .Q(register_9_q), .clk(comparator_6_eq));  // open: en, clr
  Register #(.width(32)) register_10 (.D(register_5_q), .Q(register_10_q), .clk(comparator_5_eq));  // open: en, clr
  Comparator #(.width(4), .mode("unsigned")) comparator_5 (
    .a(counter_2_q), .b(4'b1001), .eq(comparator_5_eq));  // open: gt, lt
  Multiplexer #(.width(16), .enable("false")) multiplexer_7 (
    .in0(keyscheduler_1_out_10), .in1(register_8_q[15:0]), .out(multiplexer_7_out), .sel(nor_1_out));
  Multiplexer #(.width(16), .enable("false")) multiplexer_8 (
    .in0(keyscheduler_1_out_11), .in1(register_9_q[31:16]), .out(multiplexer_8_out), .sel(nor_1_out));
  Multiplexer #(.width(16), .enable("false")) multiplexer_9 (
    .in0(keyscheduler_1_out_12), .in1(register_9_q[15:0]), .out(multiplexer_9_out), .sel(nor_1_out));
  Multiplexer #(.width(16), .enable("false")) multiplexer_10 (
    .in0(keyscheduler_1_out_13), .in1(register_10_q[31:16]), .out(multiplexer_10_out), .sel(nor_1_out));
  Multiplexer #(.width(16), .enable("false")) multiplexer_11 (
    .in0(keyscheduler_1_out_14), .in1(register_10_q[15:0]), .out(multiplexer_11_out), .sel(nor_1_out));
  KeyScheduler keyscheduler_1 (
    .Counter(counter_3_q), .Clock(and_1_out), .Enable(nand_1_out), .Clear(Clear), .k79_64(multiplexer_7_out),
    .k63_48(multiplexer_8_out), .k47_32(multiplexer_9_out), .k31_16(multiplexer_10_out),
    .k15_0(multiplexer_11_out), .out_10(keyscheduler_1_out_10), .out_11(keyscheduler_1_out_11),
    .out_12(keyscheduler_1_out_12), .out_13(keyscheduler_1_out_13), .out_14(keyscheduler_1_out_14));
  Comparator #(.width(4), .mode("unsigned")) comparator_6 (
    .a(counter_2_q), .b(4'b1010), .eq(comparator_6_eq));  // open: gt, lt
  Comparator #(.width(4), .mode("unsigned")) comparator_7 (
    .a(counter_2_q), .b(4'b1011), .eq(comparator_7_eq));  // open: gt, lt
  Counter #(.width(5), .max('h1f), .ongoal("stay")) counter_3 (
    .Q(counter_3_q), .carry(halt), .clk(and_1_out));  // open: load, D, count, clr
  nor nor_1 (nor_1_out, counter_3_q[0], counter_3_q[1], counter_3_q[2], counter_3_q[3], counter_3_q[4]);
  Comparator #(.width(4), .mode("unsigned")) comparator_8 (
    .a(counter_2_q), .b(4'b1111), .eq(comparator_8_eq));  // open: gt, lt
  nand nand_1 (nand_1_out, counter_3_q[0], counter_3_q[1], counter_3_q[2], counter_3_q[3], counter_3_q[4]);
endmodule

module KeyScheduler (
  input  [4:0] Counter,
  input  Clock,
  input  Enable,
  input  Clear,
  input  [15:0] k79_64,
  input  [15:0] k63_48,
  input  [15:0] k47_32,
  input  [15:0] k31_16,
  input  [15:0] k15_0,
  output [15:0] out_10,
  output [15:0] out_11,
  output [15:0] out_12,
  output [15:0] out_13,
  output [15:0] out_14
);

  wire [2:0] register_3_q;
  wire [3:0] register_1_q, register_2_q;
  wire [4:0] adder_1_out;
  wire [15:14] register_4_q;

  Adder #(.width(5)) adder_1 (.a(Counter), .b({5{1'b0}}), .out(adder_1_out));  // open: cin, cout
  assign out_12[15:11] = adder_1_out ^ {register_3_q, register_4_q};  // XOR_Gate xor_1, 5 bits wide
  S0 s0_1 (.in_1(register_1_q), .out_2(out_10[15:12]));
  S0 s0_2 (.in_1(register_2_q), .out_2(out_10[11:8]));
  Register #(.width(16)) register_1 (
    .D(k79_64), .en(Enable), .Q({out_14[12:0], register_1_q[3:1]}), .clk(Clock), .clr(Clear));
  Register #(.width(16)) register_2 (
    .D(k63_48), .en(Enable), .Q({register_1_q[0], register_2_q, out_10[7:0], out_11[15:13]}), .clk(Clock),
    .clr(Clear));
  Register #(.width(16)) register_3 (
    .D(k47_32), .en(Enable), .Q({out_11[12:0], register_3_q}), .clk(Clock), .clr(Clear));
  Register #(.width(16)) register_4 (
    .D(k31_16), .en(Enable), .Q({register_4_q, out_12[10:0], out_13[15:13]}), .clk(Clock), .clr(Clear));
  Register #(.width(16)) register_5 (
    .D(k15_0), .en(Enable), .Q({out_13[12:0], out_14[15:13]}), .clk(Clock), .clr(Clear));
endmodule

module Substitution_Layer (
  input  [31:0] in_1,
  output [31:0] out_2
);

  S7 s7_1 (.in_1(in_1[31:28]), .out_2(out_2[31:28]));
  S6 s6_1 (.in_1(in_1[27:24]), .out_2(out_2[27:24]));
  S5 s5_1 (.in_1(in_1[23:20]), .out_2(out_2[23:20]));
  S4 s4_1 (.in_1(in_1[19:16]), .out_2(out_2[19:16]));
  S3 s3_1 (.in_1(in_1[15:12]), .out_2(out_2[15:12]));
  S2 s2_1 (.in_1(in_1[11:8]), .out_2(out_2[11:8]));
  S1 s1_1 (.in_1(in_1[7:4]), .out_2(out_2[7:4]));
  S0 s0_1 (.in_1(in_1[3:0]), .out_2(out_2[3:0]));
endmodule

module AddRoundKey (
  input  [31:0] x,
  input  [15:0] in_2,
  input  [15:0] in_3,
  output [31:0] x_2
);

  assign x_2 = x ^ {in_2, in_3};  // XOR_Gate xor_1, 32 bits wide
endmodule

module Permutation_Layer (
  input  [31:0] in_1,
  output [31:0] out_2
);


  assign out_2 = {in_1[31], in_1[27], in_1[23], in_1[19], in_1[15], in_1[11], in_1[7], in_1[3], in_1[30], in_1[26], in_1[22], in_1[18], in_1[14], in_1[10], in_1[6], in_1[2], in_1[29], in_1[25], in_1[21], in_1[17], in_1[13], in_1[9], in_1[5], in_1[1], in_1[28], in_1[24], in_1[20], in_1[16], in_1[12], in_1[8], in_1[4], in_1[0]};
endmodule

module S0 (
  input  [3:0] in_1,
  output [3:0] out_2
);

  Multiplexer #(.select(4), .width(4), .enable("false")) multiplexer_1 (
    .in0(4'b0011), .in1(4'b1000), .in2(4'b1111), .in3(4'b0001), .in4(4'b1010), .in5(4'b0110), .in6(4'b0101),
    .in7(4'b1011), .in8(4'b1110), .in9(4'b1101), .in10(4'b0100), .in11(4'b0010), .in12(4'b0111),
    .in13(4'b0000), .in14(4'b1001), .in15(4'b1100), .out(out_2), .sel(in_1));
endmodule

module S1 (
  input  [3:0] in_1,
  output [3:0] out_2
);

  Multiplexer #(.select(4), .width(4), .enable("false")) multiplexer_1 (
    .in0(4'b1111), .in1(4'b1100), .in2(4'b0010), .in3(4'b0111), .in4(4'b1001), .in5(4'b0000), .in6(4'b0101),
    .in7(4'b1010), .in8(4'b0001), .in9(4'b1011), .in10(4'b1110), .in11(4'b1000), .in12(4'b0110),
    .in13(4'b1101), .in14(4'b0011), .in15(4'b0100), .out(out_2), .sel(in_1));
endmodule

module S2 (
  input  [3:0] in_1,
  output [3:0] out_2
);

  Multiplexer #(.select(4), .width(4), .enable("false")) multiplexer_1 (
    .in0(4'b1000), .in1(4'b0110), .in2(4'b0111), .in3(4'b1001), .in4(4'b0011), .in5(4'b1100), .in6(4'b1010),
    .in7(4'b1111), .in8(4'b1101), .in9(4'b0001), .in10(4'b1110), .in11(4'b0100), .in12(4'b0000),
    .in13(4'b1011), .in14(4'b0101), .in15(4'b0010), .out(out_2), .sel(in_1));
endmodule

module S3 (
  input  [3:0] in_1,
  output [3:0] out_2
);

  Multiplexer #(.select(4), .width(4), .enable("false")) multiplexer_1 (
    .in0(4'b0000), .in1(4'b1111), .in2(4'b1011), .in3(4'b1000), .in4(4'b1100), .in5(4'b1001), .in6(4'b0110),
    .in7(4'b0011), .in8(4'b1101), .in9(4'b0001), .in10(4'b0010), .in11(4'b0100), .in12(4'b1010),
    .in13(4'b0111), .in14(4'b0101), .in15(4'b1110), .out(out_2), .sel(in_1));
endmodule

module S4 (
  input  [3:0] in_1,
  output [3:0] out_2
);

  Multiplexer #(.select(4), .width(4), .enable("false")) multiplexer_1 (
    .in0(4'b0001), .in1(4'b1111), .in2(4'b1000), .in3(4'b0011), .in4(4'b1100), .in5(4'b0000), .in6(4'b1011),
    .in7(4'b0110), .in8(4'b0010), .in9(4'b0101), .in10(4'b0100), .in11(4'b1010), .in12(4'b1001),
    .in13(4'b1110), .in14(4'b0111), .in15(4'b1101), .out(out_2), .sel(in_1));
endmodule

module S5 (
  input  [3:0] in_1,
  output [3:0] out_2
);

  Multiplexer #(.select(4), .width(4), .enable("false")) multiplexer_1 (
    .in0(4'b1111), .in1(4'b0101), .in2(4'b0010), .in3(4'b1011), .in4(4'b0100), .in5(4'b1010), .in6(4'b1001),
    .in7(4'b1100), .in8(4'b0000), .in9(4'b0011), .in10(4'b1110), .in11(4'b1000), .in12(4'b1101),
    .in13(4'b0110), .in14(4'b0111), .in15(4'b0001), .out(out_2), .sel(in_1));
endmodule

module S6 (
  input  [3:0] in_1,
  output [3:0] out_2
);

  Multiplexer #(.select(4), .width(4), .enable("false")) multiplexer_1 (
    .in0(4'b0111), .in1(4'b0010), .in2(4'b1100), .in3(4'b0101), .in4(4'b1000), .in5(4'b0100), .in6(4'b0110),
    .in7(4'b1011), .in8(4'b1110), .in9(4'b1001), .in10(4'b0001), .in11(4'b1111), .in12(4'b1101),
    .in13(4'b0011), .in14(4'b1010), .in15(4'b0000), .out(out_2), .sel(in_1));
endmodule

module S7 (
  input  [3:0] in_1,
  output [3:0] out_2
);

  Multiplexer #(.select(4), .width(4), .enable("false")) multiplexer_1 (
    .in0(4'b0001), .in1(4'b1101), .in2(4'b1111), .in3(4'b0000), .in4(4'b1110), .in5(4'b1000), .in6(4'b0010),
    .in7(4'b1011), .in8(4'b0111), .in9(4'b0100), .in10(4'b1100), .in11(4'b1010), .in12(4'b1001),
    .in13(4'b0011), .in14(4'b0101), .in15(4'b0110), .out(out_2), .sel(in_1));
endmodule
