// Logisim project PRESENT.circ as structural Verilog: 10 circuits, main circuit main
module main (
  input  Register_Clear,
  output halt,
  output [31:0] y63_32,
  output [31:0] y31_0
);

  wire and_1_out, and_2_out, Clock_out, comparator_1_gt, comparator_2_lt, comparator_3_eq, comparator_4_eq,
       comparator_5_eq, comparator_6_eq, comparator_7_eq, comparator_8_eq, controlled_buffer_1_out,
       nand_1_out, nor_1_out, not_1_out;
  wire [2:0] counter_1_q;
  wire [3:0] counter_2_q;
  wire [4:0] Counter_3_q;
  wire [15:0] Key_Schedule_out_10, Key_Schedule_out_11, Key_Schedule_out_12, Key_Schedule_out_13,
       Key_Schedule_out_14, multiplexer_5_out, multiplexer_6_out, multiplexer_7_out, multiplexer_8_out,
       multiplexer_9_out;
  wire [31:0] Add_Round_Key_2_x31_0_2, Add_Round_Key_2_x63_32_2, Add_Round_Key_x31_0_2,
       Add_Round_Key_x63_32_2, multiplexer_1_out, multiplexer_3_out, Permutation_out_3, Permutation_out_4,
       ram_1_data, register_1_q, register_2_q, register_3_q, register_4_q, register_5_q, register_8_q,
       register_9_q, register_10_q, Substitution_out_3, Substitution_out_4;

  Counter #(.width(3), .max('h7), .ongoal("stay")) counter_1 (
    .Q(counter_1_q), .clk(controlled_buffer_1_out));  // open: load, D, count, carry, clr
  assign controlled_buffer_1_out = and_1_out ? Clock_out : 1'bz;  // Controlled_Buffer controlled_buffer_1
  Clock Clock (.out(Clock_out));
  Register #(.width(32)) register_1 (.D(register_5_q), .Q(register_1_q), .clk(comparator_4_eq));  // open: en, clr
  Counter #(.width(4), .max('hf), .ongoal("stay")) counter_2 (
    .Q(counter_2_q), .clk(Clock_out));  // open: load, D, count, carry, clr
  Register #(.width(32)) register_2 (.D(register_5_q), .Q(register_2_q), .clk(comparator_3_eq));  // open: en, clr
  Multiplexer #(.width(32), .enable("false")) multiplexer_1 (
    .in0(Add_Round_Key_2_x31_0_2), .in1(Add_Round_Key_x31_0_2), .out(multiplexer_1_out), .sel(nor_1_out));
  Register #(.width(32)) register_3 (
    .D(Permutation_out_4), .en(nand_1_out), .Q(register_3_q), .clk(and_2_out));  // open: clr
  Multiplexer #(.width(32), .enable("false")) multiplexer_2 (
    .in0(Add_Round_Key_2_x63_32_2), .out(y63_32), .sel(nand_1_out));  // open: in1
  Add_Round_Key Add_Round_Key (
    .in_1(register_10_q[15:0]), .in_2(register_8_q[31:16]), .x63_32(register_1_q), .x31_0(register_2_q),
    .in_5(register_8_q[15:0]), .in_6(register_9_q[31:16]), .x63_32_2(Add_Round_Key_x63_32_2),
    .x31_0_2(Add_Round_Key_x31_0_2));
  Multiplexer #(.width(32), .enable("false")) multiplexer_3 (
    .in0(Add_Round_Key_2_x63_32_2), .in1(Add_Round_Key_x63_32_2), .out(multiplexer_3_out), .sel(nor_1_out));
  Substitution_Layer Substitution (
    .in_1(multiplexer_3_out), .in_2(multiplexer_1_out), .out_3(Substitution_out_3), .out_4(Substitution_out_4));
  Permutation_Layer Permutation (
    .in_1(Substitution_out_3), .in_2(Substitution_out_4), .out_3(Permutation_out_3), .out_4(Permutation_out_4));
  Register #(.width(32)) register_4 (
    .D(Permutation_out_3), .en(nand_1_out), .Q(register_4_q), .clk(and_2_out));  // open: clr
  Add_Round_Key Add_Round_Key_2 (
    .in_1(Key_Schedule_out_10), .in_2(Key_Schedule_out_11), .x63_32(register_4_q), .x31_0(register_3_q),
    .in_5(Key_Schedule_out_12), .in_6(Key_Schedule_out_13), .x63_32_2(Add_Round_Key_2_x63_32_2),
    .x31_0_2(Add_Round_Key_2_x31_0_2));
  RAM #(.addrWidth(3), .dataWidth(32), .bus("separate")) ram_1 (
    .addr(counter_1_q), .data(ram_1_data), .sel(1'b1), .ld(and_1_out));  // open: din, str, clk, clr
  Comparator #(.width(4), .mode("unsigned")) comparator_1 (
    .a(counter_2_q), .b(4'b0101), .gt(comparator_1_gt));  // open: eq, lt
  Comparator #(.width(4), .mode("unsigned")) comparator_2 (
    .a(counter_2_q), .b(4'b1011), .lt(comparator_2_lt));  // open: gt, eq
  Register #(.width(32)) register_5 (.D(ram_1_data), .Q(register_5_q), .clk(controlled_buffer_1_out));  // open: en, clr
  and and_1 (and_1_out, comparator_1_gt, comparator_2_lt);
  Multiplexer #(.width(32), .enable("false")) multiplexer_4 (
    .in0(Add_Round_Key_2_x31_0_2), .out(y31_0), .sel(nand_1_out));  // open: in1
  Comparator #(.width(4), .mode("unsigned")) comparator_3 (
    .a(counter_2_q), .b(4'b0111), .eq(comparator_3_eq));  // open: gt, lt
  Register #(.width(32)) register_6 (.D(Add_Round_Key_2_x63_32_2), .clk(and_2_out));  // open: en, Q, clr
  Multiplexer #(.width(16), .enable("false")) multiplexer_5 (
    .in0(register_10_q[15:0]), .in1(Key_Schedule_out_10), .out(multiplexer_5_out), .sel(not_1_out));
  Multiplexer #(.width(16), .enable("false")) multiplexer_6 (
    .in0(register_8_q[31:16]), .in1(Key_Schedule_out_11), .out(multiplexer_6_out), .sel(not_1_out));
  Multiplexer #(.width(16), .enable("false")) multiplexer_7 (
    .in0(register_8_q[15:0]), .in1(Key_Schedule_out_12), .out(multiplexer_7_out), .sel(not_1_out));
  Multiplexer #(.width(16), .enable("false")) multiplexer_8 (
    .in0(register_9_q[31:16]), .in1(Key_Schedule_out_13), .out(multiplexer_8_out), .sel(not_1_out));
  Multiplexer #(.width(16), .enable("false")) multiplexer_9 (
    .in0(register_9_q[15:0]), .in1(Key_Schedule_out_14), .out(multiplexer_9_out), .sel(not_1_out));
  Register #(.width(32)) register_7 (.D(Add_Round_Key_2_x31_0_2), .clk(and_2_out));  // open: en, Q, clr
  Comparator #(.width(4), .mode("unsigned")) comparator_4 (
    .a(counter_2_q), .b(4'b1000), .eq(comparator_4_eq));  // open: gt, lt
  Comparator #(.width(4), .mode("unsigned")) comparator_5 (
    .a(counter_2_q), .b(4'b1001), .eq(comparator_5_eq));  // open: gt, lt
  and and_2 (and_2_out, Clock_out, comparator_8_eq);
  Key_Schedule Key_Schedule (
    .Counter(Counter_3_q), .Register_Enable(nand_1_out), .Clock(and_2_out), .Register_Clear(Register_Clear),
    .InputKey79_64(multiplexer_5_out), .InputKey63_48(multiplexer_6_out), .InputKey47_32(multiplexer_7_out),
    .InputKey31_16(multiplexer_8_out), .InputKey15_0(multiplexer_9_out), .out_10(Key_Schedule_out_10),
    .out_11(Key_Schedule_out_11), .out_12(Key_Schedule_out_12), .out_13(Key_Schedule_out_13),
    .out_14(Key_Schedule_out_14));
  Comparator #(.width(4), .mode("unsigned")) comparator_6 (
    .a(counter_2_q), .b(4'b1010), .eq(comparator_6_eq));  // open: gt, lt
  Counter #(.width(5), .max('h1f), .ongoal("stay")) Counter_3 (
    .Q(Counter_3_q), .carry(halt), .clk(and_2_out));  // open: load, D, count, clr
  Register #(.width(32)) register_8 (.D(register_5_q), .Q(register_8_q), .clk(comparator_6_eq));  // open: en, clr
  Comparator #(.width(4), .mode("unsigned")) comparator_7 (
    .a(counter_2_q), .b(4'b1011), .eq(comparator_7_eq));  // open: gt, lt
  Register #(.width(32)) register_9 (.D(register_5_q), .Q(register_9_q), .clk(comparator_5_eq));  // open: en, clr
  Comparator #(.width(4), .mode("unsigned")) comparator_8 (
    .a(counter_2_q), .b(4'b1111), .eq(comparator_8_eq));  // open: gt, lt
  nor nor_1 (nor_1_out, Counter_3_q[4], Counter_3_q[3], Counter_3_q[2], Counter_3_q[1], Counter_3_q[0]);
  not not_1 (not_1_out, nor_1_out);
  Register #(.width(32)) register_10 (.D(register_5_q), .Q(register_10_q), .clk(comparator_7_eq));  // open: en, clr
  nand nand_1 (nand_1_out, Counter_3_q[0], Counter_3_q[1], Counter_3_q[2], Counter_3_q[3], Counter_3_q[4]);
endmodule

module Key_Schedule (
  input  [4:0] Counter,
  input  Register_Enable,
  input  Clock,
  input  Register_Clear,
  input  [15:0] InputKey79_64,
  input  [15:0] InputKey63_48,
  input  [15:0] InputKey47_32,
  input  [15:0] InputKey31_16,
  input  [15:0] InputKey15_0,
  output [15:0] out_10,
  output [15:0] out_11,
  output [15:0] out_12,
  output [15:0] out_13,
  output [15:0] out_14
);

  wire [2:0] register_4_q;
  wire [4:0] adder_1_out;
  wire [6:2] register_3_q;
  wire [15:15] register_5_q;

  Adder #(.width(5)) adder_1 (.a(Counter), .b({5{1'b0}}), .out(adder_1_out));  // open: cin, cout
  assign {out_13[3:0], out_14[15]} = register_3_q ^ adder_1_out;  // XOR_Gate xor_1, 5 bits wide
  Substitution_Block substitution_block_1 (
    .in_1(register_4_q[2]), .in_2(register_4_q[1]), .in_3(register_4_q[0]), .in_4(register_5_q[15]),
    .out_5(out_10[15]), .out_6(out_10[14]), .out_7(out_10[13]), .out_8(out_10[12]));
  Register #(.width(16)) register_1 (
    .D(InputKey79_64), .en(Register_Enable), .Q({out_11[12:0], out_12[15:13]}), .clk(Clock),
    .clr(Register_Clear));
  Register #(.width(16)) register_2 (
    .D(InputKey63_48), .en(Register_Enable), .Q({out_12[12:0], out_13[15:13]}), .clk(Clock),
    .clr(Register_Clear));
  Register #(.width(16)) register_3 (
    .D(InputKey47_32), .en(Register_Enable), .Q({out_13[12:4], register_3_q, out_14[14:13]}), .clk(Clock),
    .clr(Register_Clear));
  Register #(.width(16)) register_4 (
    .D(InputKey31_16), .en(Register_Enable), .Q({out_14[12:0], register_4_q}), .clk(Clock),
    .clr(Register_Clear));
  Register #(.width(16)) register_5 (
    .D(InputKey15_0), .en(Register_Enable), .Q({register_5_q[15], out_10[11:0], out_11[15:13]}), .clk(Clock),
    .clr(Register_Clear));
endmodule

module Substitution_Layer (
  input  [31:0] in_1,
  input  [31:0] in_2,
  output [31:0] out_3,
  output [31:0] out_4
);

  Substitution_Block substitution_block_1 (
    .in_1(in_1[31]), .in_2(in_1[30]), .in_3(in_1[29]), .in_4(in_1[28]), .out_5(out_3[31]), .out_6(out_3[30]),
    .out_7(out_3[29]), .out_8(out_3[28]));
  Substitution_Block substitution_block_2 (
    .in_1(in_1[27]), .in_2(in_1[26]), .in_3(in_1[25]), .in_4(in_1[24]), .out_5(out_3[27]), .out_6(out_3[26]),
    .out_7(out_3[25]), .out_8(out_3[24]));
  Substitution_Block substitution_block_3 (
    .in_1(in_1[23]), .in_2(in_1[22]), .in_3(in_1[21]), .in_4(in_1[20]), .out_5(out_3[23]), .out_6(out_3[22]),
    .out_7(out_3[21]), .out_8(out_3[20]));
  Substitution_Block substitution_block_4 (
    .in_1(in_1[19]), .in_2(in_1[18]), .in_3(in_1[17]), .in_4(in_1[16]), .out_5(out_3[19]), .out_6(out_3[18]),
    .out_7(out_3[17]), .out_8(out_3[16]));
  Substitution_Block substitution_block_5 (
    .in_1(in_1[15]), .in_2(in_1[14]), .in_3(in_1[13]), .in_4(in_1[12]), .out_5(out_3[15]), .out_6(out_3[14]),
    .out_7(out_3[13]), .out_8(out_3[12]));
  Substitution_Block substitution_block_6 (
    .in_1(in_1[11]), .in_2(in_1[10]), .in_3(in_1[9]), .in_4(in_1[8]), .out_5(out_3[11]), .out_6(out_3[10]),
    .out_7(out_3[9]), .out_8(out_3[8]));
  Substitution_Block substitution_block_7 (
    .in_1(in_1[7]), .in_2(in_1[6]), .in_3(in_1[5]), .in_4(in_1[4]), .out_5(out_3[7]), .out_6(out_3[6]),
    .out_7(out_3[5]), .out_8(out_3[4]));
  Substitution_Block substitution_block_8 (
    .in_1(in_1[3]), .in_2(in_1[2]), .in_3(in_1[1]), .in_4(in_1[0]), .out_5(out_3[3]), .out_6(out_3[2]),
    .out_7(out_3[1]), .out_8(out_3[0]));
  Substitution_Block substitution_block_9 (
    .in_1(in_2[31]), .in_2(in_2[30]), .in_3(in_2[29]), .in_4(in_2[28]), .out_5(out_4[31]), .out_6(out_4[30]),
    .out_7(out_4[29]), .out_8(out_4[28]));
  Substitution_Block substitution_block_10 (
    .in_1(in_2[27]), .in_2(in_2[26]), .in_3(in_2[25]), .in_4(in_2[24]), .out_5(out_4[27]), .out_6(out_4[26]),
    .out_7(out_4[25]), .out_8(out_4[24]));
  Substitution_Block substitution_block_11 (
    .in_1(in_2[23]), .in_2(in_2[22]), .in_3(in_2[21]), .in_4(in_2[20]), .out_5(out_4[23]), .out_6(out_4[22]),
    .out_7(out_4[21]), .out_8(out_4[20]));
  Substitution_Block substitution_block_12 (
    .in_1(in_2[19]), .in_2(in_2[18]), .in_3(in_2[17]), .in_4(in_2[16]), .out_5(out_4[19]), .out_6(out_4[18]),
    .out_7(out_4[17]), .out_8(out_4[16]));
  Substitution_Block substitution_block_13 (
    .in_1(in_2[15]), .in_2(in_2[14]), .in_3(in_2[13]), .in_4(in_2[12]), .out_5(out_4[15]), .out_6(out_4[14]),
    .out_7(out_4[13]), .out_8(out_4[12]));
  Substitution_Block substitution_block_14 (
    .in_1(in_2[11]), .in_2(in_2[10]), .in_3(in_2[9]), .in_4(in_2[8]), .out_5(out_4[11]), .out_6(out_4[10]),
    .out_7(out_4[9]), .out_8(out_4[8]));
  Substitution_Block substitution_block_15 (
    .in_1(in_2[7]), .in_2(in_2[6]), .in_3(in_2[5]), .in_4(in_2[4]), .out_5(out_4[7]), .out_6(out_4[6]),
    .out_7(out_4[5]), .out_8(out_4[4]));
  Substitution_Block substitution_block_16 (
    .in_1(in_2[3]), .in_2(in_2[2]), .in_3(in_2[1]), .in_4(in_2[0]), .out_5(out_4[3]), .out_6(out_4[2]),
    .out_7(out_4[1]), .out_8(out_4[0]));
endmodule

module Permutation_Layer (
  input  [31:0] in_1,
  input  [31:0] in_2,
  output [31:0] out_3,
  output [31:0] out_4
);


  assign out_3 = {in_1[31], in_1[27], in_1[23], in_1[19], in_1[15], in_1[11], in_1[7], in_1[3], in_2[31], in_2[27], in_2[23], in_2[19], in_2[15], in_2[11], in_2[7], in_2[3], in_1[30], in_1[26], in_1[22], in_1[18], in_1[14], in_1[10], in_1[6], in_1[2], in_2[30], in_2[26], in_2[22], in_2[18], in_2[14], in_2[10], in_2[6], in_2[2]};
  assign out_4 = {in_1[29], in_1[25], in_1[21], in_1[17], in_1[13], in_1[9], in_1[5], in_1[1], in_2[29], in_2[25], in_2[21], in_2[17], in_2[13], in_2[9], in_2[5], in_2[1], in_1[28], in_1[24], in_1[20], in_1[16], in_1[12], in_1[8], in_1[4], in_1[0], in_2[28], in_2[24], in_2[20], in_2[16], in_2[12], in_2[8], in_2[4], in_2[0]};
endmodule

module Add_Round_Key (
  input  [15:0] in_1,
  input  [15:0] in_2,
  input  [31:0] x63_32,
  input  [31:0] x31_0,
  input  [15:0] in_5,
  input  [15:0] in_6,
  output [31:0] x63_32_2,
  output [31:0] x31_0_2
);

  assign x63_32_2 = x63_32 ^ {in_1, in_2};  // XOR_Gate xor_1, 32 bits wide
  assign x31_0_2 = x31_0 ^ {in_5, in_6};  // XOR_Gate xor_2, 32 bits wide
endmodule

module Substitution_Block (
  input  in_1,
  input  in_2,
  input  in_3,
  input  in_4,
  output out_5,
  output out_6,
  output out_7,
  output out_8
);

  wire not_1_out, not_2_out, not_3_out, not_4_out;

  not not_1 (not_1_out, in_1);
  not not_2 (not_2_out, in_2);
  not not_3 (not_3_out, in_3);
  not not_4 (not_4_out, in_4);
  y3 y3_1 (
    .in_1(not_1_out), .in_2(in_1), .in_3(not_2_out), .in_4(in_2), .in_5(not_3_out), .in_6(in_3),
    .in_7(not_4_out), .in_8(in_4), .out_9(out_5));
  y2 y2_1 (
    .in_1(not_1_out), .in_2(in_1), .in_3(not_2_out), .in_4(in_2), .in_5(not_3_out), .in_6(in_3),
    .in_7(not_4_out), .in_8(in_4), .out_9(out_6));
  y1 y1_1 (
    .in_1(not_1_out), .in_2(in_1), .in_3(not_2_out), .in_4(in_2), .in_5(not_3_out), .in_6(in_3),
    .in_7(not_4_out), .in_8(in_4), .out_9(out_7));
  y0 y0_1 (
    .in_1(not_1_out), .in_2(in_1), .in_3(not_2_out), .in_4(in_2), .in_5(not_3_out), .in_6(in_3),
    .in_7(not_4_out), .in_8(in_4), .out_9(out_8));
endmodule

module y3 (
  input  in_1,
  input  in_2,
  input  in_3,
  input  in_4,
  input  in_5,
  input  in_6,
  input  in_7,
  input  in_8,
  output out_9
);

  wire and_1_out, and_2_out, and_3_out, and_4_out, and_5_out;

  and and_1 (and_1_out, in_1, in_5, in_7);
  and and_2 (and_2_out, in_2, in_3, in_6);
  and and_3 (and_3_out, in_2, in_3, in_8);
  and and_4 (and_4_out, in_1, in_4, in_6);
  and and_5 (and_5_out, in_1, in_6, in_8);
  or or_1 (out_9, and_1_out, and_2_out, and_3_out, and_4_out, and_5_out);
endmodule

module y2 (
  input  in_1,
  input  in_2,
  input  in_3,
  input  in_4,
  input  in_5,
  input  in_6,
  input  in_7,
  input  in_8,
  output out_9
);

  wire and_1_out, and_2_out, and_3_out, and_4_out, and_5_out;

  and and_1 (and_1_out, in_1, in_4, in_6, in_8);
  and and_2 (and_2_out, in_1, in_3, in_5);
  and and_3 (and_3_out, in_3, in_6, in_7);
  and and_4 (and_4_out, in_2, in_4, in_5);
  and and_5 (and_5_out, in_2, in_5, in_8);
  or or_1 (out_9, and_1_out, and_2_out, and_3_out, and_4_out, and_5_out);
endmodule

module y1 (
  input  in_1,
  input  in_2,
  input  in_3,
  input  in_4,
  input  in_5,
  input  in_6,
  input  in_7,
  input  in_8,
  output out_9
);

  wire and_1_out, and_2_out, and_3_out, and_4_out, and_5_out;

  and and_1 (and_1_out, in_2, in_3, in_5);
  and and_2 (and_2_out, in_3, in_6, in_7);
  and and_3 (and_3_out, in_1, in_6, in_7);
  and and_4 (and_4_out, in_1, in_3, in_6);
  and and_5 (and_5_out, in_2, in_4, in_8);
  or or_1 (out_9, and_1_out, and_2_out, and_3_out, and_4_out, and_5_out);
endmodule

module y0 (
  input  in_1,
  input  in_2,
  input  in_3,
  input  in_4,
  input  in_5,
  input  in_6,
  input  in_7,
  input  in_8,
  output out_9
);

  wire and_1_out, and_2_out, and_3_out, and_4_out, and_5_out, and_6_out;

  and and_1 (and_1_out, in_1, in_4, in_5, in_7);
  and and_2 (and_2_out, in_2, in_4, in_5, in_8);
  and and_3 (and_3_out, in_2, in_3, in_7);
  and and_4 (and_4_out, in_1, in_3, in_8);
  and and_5 (and_5_out, in_2, in_6, in_7);
  and and_6 (and_6_out, in_1, in_6, in_8);
  or or_1 (out_9, and_1_out, and_2_out, and_3_out, and_4_out, and_5_out, and_6_out);
endmodule
